# Fritzing sketch mptcc_v1.1 (saved by Fritzing 1.0.4)
breadboards: 4

parts:
  MC = Raspberry Pi Pico2
  RE1 = KY-040 Rotary encoder [package=THT]
  RE2 = KY-040 Rotary encoder [package=THT]
  RE3 = KY-040 Rotary encoder [package=THT]
  RE4 = KY-040 Rotary encoder [package=THT]
  Q1 = NPN-Transistor [part_number=2N4401 package="TO92 [THT]"]
  Q2 = NPN-Transistor [part_number=2N4401 package="TO92 [THT]"]
  Q3 = NPN-Transistor [part_number=2N4401 package="TO92 [THT]"]
  Q4 = NPN-Transistor [part_number=2N4401 package="TO92 [THT]"]
  J1 = MIDI_CONN_FEMALE [package=din_5_female]
  LED1 = LED - 5mm [color="Infrared (940nm)" current=0.030A package="5 mm [THT]"]
  M1 = OLED Mono 2.42 inch green
  U2 = Adafruit PCA9685 PWM/Servo Breakout [part_number=815]
  LED5 = RGB LED (com. cathode, rgb) [color="Red (633nm)" current=0.030A package="5 mm [THT]"]
  LED6 = RGB LED (com. cathode, rgb) [color="Red (633nm)" current=0.030A package="5 mm [THT]"]
  LED7 = RGB LED (com. cathode, rgb) [color="Red (633nm)" current=0.030A package="5 mm [THT]"]
  LED8 = RGB LED (com. cathode, rgb) [color="Red (633nm)" current=0.030A package="5 mm [THT]"]
  LED2 = LED - 5mm [color="Infrared (940nm)" current=0.030A package="5 mm [THT]"]
  LED3 = LED - 5mm [color="Infrared (940nm)" current=0.030A package="5 mm [THT]"]
  LED4 = LED - 5mm [color="Infrared (940nm)" current=0.030A package="5 mm [THT]"]
  U1 = IC, DIP package, 8 pins [chip_label=6N138]
  D1 = Diode [package=diode-1n4148]
  R7 = Resistor [tolerance=±1% power=0.25W resistance=470 package=THT]
  R5 = Resistor [tolerance=±1% power=0.25W resistance=470 package=THT]
  R6 = Resistor [tolerance=±1% power=0.25W resistance=470 package=THT]
  R8 = Resistor [tolerance=±1% power=0.25W resistance=470 package=THT]
  R10 = Resistor [tolerance=±1% power=0.25W resistance=220 package=THT]
  R9 = Resistor [tolerance=±1% power=0.25W resistance=470 package=THT]
  R1 = Resistor [tolerance=±1% power=0.25W resistance=100 package=THT]
  R2 = Resistor [tolerance=±1% power=0.25W resistance=100 package=THT]
  R3 = Resistor [tolerance=±1% power=0.25W resistance=100 package=THT]
  R4 = Resistor [tolerance=±1% power=0.25W resistance=100 package=THT]
  SD1 = Full Size SD Card Module
  R11 = Resistor [tolerance=±1% power=0.25W resistance=4.7k package=THT]
  R12 = Resistor [tolerance=±1% power=0.25W resistance=4.7k package=THT]
  R13 = Resistor [tolerance=±1% power=0.25W resistance=20k package=THT]
  R14 = Resistor [tolerance=±1% power=0.25W resistance=75k package=THT]
  JP1 = Header 1 [package=smtso-256-et]
  JP2 = Header 1 [package=smtso-256-et]
  R15 = Resistor [tolerance=±1% power=0.25W resistance=4.7k package=THT]
  R16 = Resistor [tolerance=±1% power=0.25W resistance=4.7k package=THT]

nets:
  N1: MC.pin_1, RE3.SW
  N2: MC.pin_2, SD1.pin_7, SD1.pin_8
  GND: MC.pin_3, MC.pin_8, MC.pin_13, MC.pin_18, MC.pin_23, MC.pin_28, MC.pin_33, MC.pin_38, RE1.GND, RE2.GND, RE3.GND, RE4.GND, Q1.E, Q2.E, Q3.E, Q4.E, M1.GND, U2.GND, LED5.common_cathode, LED6.common_cathode, LED7.common_cathode, LED8.common_cathode, U1.pin5, SD1.pin_1, SD1.pin_2, SD1.pin_15, SD1.pin_16, R13.Pin_1
  N3: MC.pin_4, SD1.pin_11, SD1.pin_12
  N4: MC.pin_5, SD1.pin_9, SD1.pin_10
  N5: MC.pin_6, SD1.pin_13, SD1.pin_14
  N6: MC.pin_7, RE4.SW
  N7: MC.pin_9, R5.Pin_1
  N8: MC.pin_10, R7.Pin_1
  N9: MC.pin_11, R8.Pin_1
  N10: MC.pin_12, RE2.CLK
  N11: MC.pin_14, RE1.CLK
  N12: MC.pin_15, RE1.DT
  N13: MC.pin_16, RE1.SW
  N14: MC.pin_17, U1.pin6, R9.Pin_1
  N15: MC.pin_19, RE2.DT
  N16: MC.pin_20, RE2.SW
  N17: MC.pin_21, M1.SDA, R15.Pin_0
  N18: MC.pin_22, M1.SCL, R16.Pin_0
  N19: MC.pin_24, U2.SDA, R11.Pin_0
  N20: MC.pin_25, U2.SCL, R12.Pin_0
  N21: MC.pin_26, RE4.DT
  N22: MC.pin_27, RE4.CLK
  N23: MC.pin_29, R6.Pin_1
  N24: MC.pin_31, RE3.DT
  N25: MC.pin_32, RE3.CLK
  N26: MC.pin_34, R13.Pin_0, R14.Pin_1
  VCC: MC.pin_36, RE1.Vcc, RE2.Vcc, RE3.Vcc, RE4.Vcc, M1.VCC, U2.VCC, SD1.pin_3, SD1.pin_4, R11.Pin_1, R12.Pin_1, R15.Pin_1, R16.Pin_1
  N27: Q1.B, R5.Pin_0
  N28: Q1.C, R1.Pin_0
  N29: Q2.B, R6.Pin_0
  N30: Q2.C, R2.Pin_0
  N31: Q3.B, R7.Pin_0
  N32: Q3.C, R3.Pin_0
  N33: Q4.B, R8.Pin_0
  N34: Q4.C, R4.Pin_0
  N35: J1.MIDI_IN, R10.Pin_0
  N36: J1.MIDI_OUT, U1.pin3, D1.A
  N37: LED1.cathode, R1.Pin_1
  N38: LED1.anode, LED2.anode, LED3.anode, LED4.anode, U1.pin8, R9.Pin_0, JP2.1
  N39: U2.PWM7, LED7.green_anode
  N40: U2.PWM6, LED7.red_anode
  N41: U2.PWM5, LED6.blue_anode
  N42: U2.PWM4, LED6.green_anode
  N43: U2.PWM3, LED6.red_anode
  N44: U2.PWM2, LED5.blue_anode
  N45: U2.PWM1, LED5.green_anode
  N46: U2.PWM0, LED5.red_anode
  N47: U2.PWM11, LED8.blue_anode
  N48: U2.PWM10, LED8.green_anode
  N49: U2.PWM9, LED8.red_anode
  N50: U2.PWM8, LED7.blue_anode
  N51: LED2.cathode, R2.Pin_1
  N52: LED3.cathode, R3.Pin_1
  N53: LED4.cathode, R4.Pin_1
  N54: U1.pin2, D1.C, R10.Pin_1
  N55: SD1.pin_5, SD1.pin_6
  N56: R14.Pin_0, JP1.1

custom parts:
  Raspberry Pi Pico2: Raspberry Pi Pico 2 is our new $5 microcontroller board, built on RP2350: our new high-performance, secure microcontroller.
  KY-040 Rotary encoder: KY-040 Rotary Encoder with switch on breakout borad from AZ Delivery
  OLED Mono 2.42 inch green: This is a 2.42 inch OLED display module of 128x64 resolution.
  Adafruit PCA9685 PWM/Servo Breakout: Using only two pins, control 16 free-running PWM outputs! I2C-controlled PWM driver with a built in clock. Unlike the TLC5940 family, you do not need to continuously send it signal tying up your microcontroller, its completely free running! 5V compliant, which means you can control it from a 3.3V microcontroller and still safely drive up to 6V outputs (this is good for when you want to control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
  Full Size SD Card Module: SD Card Module Slot Socket Reader For Arduino ARM MCU
